// Logisim project minirv.circ as structural Verilog: 11 circuits, main circuit minirv
module minirv (
  input  reset
);

  wire clock_1_out, executor_1_jump_enable, executor_1_wenable;
  wire [4:0] executor_1_raddr1, executor_1_raddr2, executor_1_waddr;
  wire [31:0] executor_1_jump_addr, executor_1_wdata, fetcher_1_instruction, fetcher_1_next_addr,
       gpr_32x32bit_1_rdata1, gpr_32x32bit_1_rdata2;

  Clock clock_1 (.out(clock_1_out));
  fetcher fetcher_1 (
    .jump_addr(executor_1_jump_addr), .jump_enable(executor_1_jump_enable), .clk(clock_1_out), .reset(reset),
    .next_addr(fetcher_1_next_addr), .instruction(fetcher_1_instruction));
  GPR_32x32bit gpr_32x32bit_1 (
    .clk(clock_1_out), .wdata(executor_1_wdata), .waddr(executor_1_waddr), .wenable(executor_1_wenable),
    .reset(reset), .raddr1(executor_1_raddr1), .raddr2(executor_1_raddr2), .rdata1(gpr_32x32bit_1_rdata1),
    .rdata2(gpr_32x32bit_1_rdata2));
  executor executor_1 (
    .instruction(fetcher_1_instruction), .rdata1(gpr_32x32bit_1_rdata1), .rdata2(gpr_32x32bit_1_rdata2),
    .next_addr(fetcher_1_next_addr), .raddr1(executor_1_raddr1), .raddr2(executor_1_raddr2),
    .waddr(executor_1_waddr), .wenable(executor_1_wenable), .wdata(executor_1_wdata),
    .jump_addr(executor_1_jump_addr), .jump_enable(executor_1_jump_enable));
endmodule

module instruction_type_detector (
  input  [31:0] instruction,
  output is_i_load,
  output is_i_compute,
  output is_i,
  output is_i_jump,
  output is_r
);

  Comparator #(.mode("unsigned"), .width(7)) comparator_1 (
    .a(7'b0000011), .b(instruction[6:0]), .eq(is_i_load));  // open: gt, lt
  Comparator #(.mode("unsigned"), .width(7)) comparator_2 (
    .a(7'b0010011), .b(instruction[6:0]), .eq(is_i_compute));  // open: gt, lt
  Comparator #(.mode("unsigned"), .width(7)) comparator_3 (
    .a(7'b1100111), .b(instruction[6:0]), .eq(is_i_jump));  // open: gt, lt
  Comparator #(.mode("unsigned"), .width(7)) comparator_4 (
    .a(instruction[6:0]), .b(7'b0110011), .eq(is_r));  // open: gt, lt
  or or_1 (is_i, is_i_load, is_i_compute, is_i_jump);
endmodule

module i_decoder (
  input  [31:0] instruction,
  output [6:0] opcode,
  output [4:0] rd,
  output [2:0] funct3,
  output [6:0] funct7,
  output [4:0] rs1,
  output [4:0] rs2,
  output [11:0] imm
);


  assign funct3 = instruction[14:12];
  assign funct7 = {7{1'b0}};
  assign imm = instruction[31:20];
  assign opcode = instruction[6:0];
  assign rd = instruction[11:7];
  assign rs1 = instruction[19:15];
  assign rs2 = {5{1'b0}};
endmodule

module instruction_decoder (
  input  [31:0] instrction,
  output [6:0] opcode,
  output [4:0] rd,
  output [2:0] funct3,
  output [4:0] rs1,
  output [11:0] imm,
  output [6:0] funct7,
  output [4:0] rs2
);

  wire instruction_type_detector_1_is_i, instruction_type_detector_1_is_r, or_1_out, priority_encoder_1_out,
       select_signal;
  wire [2:0] i_funct3, r_funct3;
  wire [4:0] i_rd, i_rs1, i_rs2, r_rd, r_rs1, r_rs2;
  wire [6:0] i_funct7, i_opcode, r_funct7, r_opcode;
  wire [11:0] i_imm, r_imm;

  instruction_type_detector instruction_type_detector_1 (
    .instruction(instrction), .is_i(instruction_type_detector_1_is_i), .is_r(instruction_type_detector_1_is_r));  // open: is_i_load, is_i_compute, is_i_jump
  i_decoder i_decoder_1 (
    .instruction(instrction), .opcode(i_opcode), .rd(i_rd), .funct3(i_funct3), .funct7(i_funct7),
    .rs1(i_rs1), .rs2(i_rs2), .imm(i_imm));
  r_decoder r_decoder_1 (
    .instruction(instrction), .opcode(r_opcode), .rd(r_rd), .funct3(r_funct3), .rs1(r_rs1), .rs2(r_rs2),
    .funct7(r_funct7), .imm(r_imm));
  or or_1 (or_1_out, instruction_type_detector_1_is_i, instruction_type_detector_1_is_r);
  Priority_Encoder #(.select(1)) priority_encoder_1 (
    .in0(instruction_type_detector_1_is_i), .in1(instruction_type_detector_1_is_r),
    .out(priority_encoder_1_out));  // open: gs, en_out, en_in
  Multiplexer multiplexer_1 (.in0(1'b0), .in1(priority_encoder_1_out), .out(select_signal), .sel(or_1_out));
  Multiplexer #(.width(7)) multiplexer_2 (.in0(i_opcode), .in1(r_opcode), .out(opcode), .sel(select_signal));
  Multiplexer #(.width(5)) multiplexer_3 (.in0(i_rd), .in1(r_rd), .out(rd), .sel(select_signal));
  Multiplexer #(.width(3)) multiplexer_4 (.in0(i_funct3), .in1(r_funct3), .out(funct3), .sel(select_signal));
  Multiplexer #(.width(5)) multiplexer_5 (.in0(i_rs1), .in1(r_rs1), .out(rs1), .sel(select_signal));
  Multiplexer #(.width(12)) multiplexer_6 (.in0(i_imm), .in1(r_imm), .out(imm), .sel(select_signal));
  Multiplexer #(.width(7)) multiplexer_7 (.in0(i_funct7), .in1(r_funct7), .out(funct7), .sel(select_signal));
  Multiplexer #(.width(5)) multiplexer_8 (.in0(i_rs2), .in1(r_rs2), .out(rs2), .sel(select_signal));

  // Other names for the same wires on the sheet: instruction[31:0] = instrction
endmodule

module instruction_identifier (
  input  [31:0] instruction,
  output is_addi,
  output is_jalr,
  output is_add
);

  wire and_1_out, comparator_1_eq, comparator_2_eq, comparator_3_eq, comparator_4_eq,
       instruction_type_detector_1_is_i_compute, instruction_type_detector_1_is_i_jump,
       instruction_type_detector_1_is_r;
  wire [2:0] instruction_decoder_1_funct3;
  wire [6:0] instruction_decoder_1_funct7;

  instruction_decoder instruction_decoder_1 (
    .instrction(instruction), .funct3(instruction_decoder_1_funct3), .funct7(instruction_decoder_1_funct7));  // open: opcode, rd, rs1, imm, rs2
  Comparator #(.mode("unsigned"), .width(3)) comparator_1 (
    .a(instruction_decoder_1_funct3), .b(3'b000), .eq(comparator_1_eq));  // open: gt, lt
  Comparator #(.mode("unsigned"), .width(3)) comparator_2 (
    .a(instruction_decoder_1_funct3), .b(3'b000), .eq(comparator_2_eq));  // open: gt, lt
  Comparator #(.mode("unsigned"), .width(3)) comparator_3 (
    .a(instruction_decoder_1_funct3), .b(3'b000), .eq(comparator_3_eq));  // open: gt, lt
  Comparator #(.mode("unsigned"), .width(7)) comparator_4 (
    .a(instruction_decoder_1_funct7), .b({7{1'b0}}), .eq(comparator_4_eq));  // open: gt, lt
  instruction_type_detector instruction_type_detector_1 (
    .instruction(instruction), .is_i_compute(instruction_type_detector_1_is_i_compute),
    .is_i_jump(instruction_type_detector_1_is_i_jump), .is_r(instruction_type_detector_1_is_r));  // open: is_i_load, is_i
  and and_1 (and_1_out, comparator_3_eq, comparator_4_eq);
  and and_2 (is_addi, instruction_type_detector_1_is_i_compute, comparator_1_eq);
  and and_3 (is_jalr, instruction_type_detector_1_is_i_jump, comparator_2_eq);
  and and_4 (is_add, instruction_type_detector_1_is_r, and_1_out);
endmodule

module fetcher (
  input  [31:0] jump_addr,
  input  jump_enable,
  input  clk,
  input  reset,
  output [31:0] next_addr,
  output [31:0] instruction
);

  wire [7:0] rom_1_p1;
  wire [31:0] multiplexer_1_out;
  wire [31:8] PC_q;

  Multiplexer #(.width(32)) multiplexer_1 (
    .in0(next_addr), .in1(jump_addr), .out(multiplexer_1_out), .sel(jump_enable));
  // ROM #(.line("quad")) rom_1: pin names not known; wires that end beside it: rom_1_p1, instruction[7:0], instruction[15:8], instruction[23:16], instruction[31:24]
  Register #(.width(32)) PC (.D(multiplexer_1_out), .en(1'b1), .clk(clk), .Q({PC_q, rom_1_p1}), .clr(reset));
  Adder #(.width(32)) adder_1 (.a(32'h4), .b({PC_q, rom_1_p1}), .out(next_addr));  // open: cin, cout

  // Notes on the sheet:
  //   contents of rom_1 (hex, n*v repeats v):
  //   13 5 40 1 e7 0 0 1 e7 0 c0 0 67 0 c0 0 13 5 a5 0 67 80
endmodule

module executor (
  input  [31:0] instruction,
  input  [31:0] rdata1,
  input  [31:0] rdata2,
  input  [31:0] next_addr,
  output [4:0] raddr1,
  output [4:0] raddr2,
  output [4:0] waddr,
  output wenable,
  output [31:0] wdata,
  output [31:0] jump_addr,
  output jump_enable
);

  wire add_jump_enable, add_wenable, addi_jump_enable, addi_wenable, is_add, is_addi, is_jalr,
       jalr_jump_enable, jalr_wenable, or_1_out;
  wire [2:0] priority_encoder_1_out, select_signal;
  wire [4:0] add_raddr1, add_raddr2, add_waddr, addi_raddr1, addi_raddr2, addi_waddr, jalr_raddr1,
       jalr_raddr2, jalr_waddr;
  wire [31:0] add_jump_addr, add_wdata, addi_jump_addr, addi_wdata, jalr_jump_addr, jalr_wdata;

  instruction_identifier instruction_identifier_1 (
    .instruction(instruction), .is_addi(is_addi), .is_jalr(is_jalr), .is_add(is_add));
  addi_executor addi_executor_1 (
    .instruction(instruction), .rdata1(rdata1), .raddr1(addi_raddr1), .raddr2(addi_raddr2),
    .waddr(addi_waddr), .wenable(addi_wenable), .wdata(addi_wdata), .jump_addr(addi_jump_addr),
    .jump_enable(addi_jump_enable));
  jalr_excutor jalr_excutor_1 (
    .instruction(instruction), .rdata1(rdata1), .next_addr(next_addr), .raddr1(jalr_raddr1),
    .raddr2(jalr_raddr2), .waddr(jalr_waddr), .wenable(jalr_wenable), .wdata(jalr_wdata),
    .jump_addr(jalr_jump_addr), .jump_enable(jalr_jump_enable));
  add_executor add_executor_1 (
    .instruction(instruction), .rdata1(rdata1), .rdata2(rdata2), .raddr1(add_raddr1), .raddr2(add_raddr2),
    .waddr(add_waddr), .wenable(add_wenable), .wdata(add_wdata), .jump_addr(add_jump_addr),
    .jump_enable(add_jump_enable));
  Priority_Encoder priority_encoder_1 (
    .in0(is_addi), .in1(is_jalr), .in2(is_add), .in3(1'b0), .in4(1'b0), .in5(1'b0), .in6(1'b0), .in7(1'b0),
    .out(priority_encoder_1_out));  // open: en_in, gs, en_out
  or or_1 (or_1_out, is_addi, is_jalr, is_add);
  Multiplexer #(.select(3), .width(5)) multiplexer_1 (
    .in0(addi_raddr1), .in1(jalr_raddr1), .in2(add_raddr1), .in3({5{1'b0}}), .in4({5{1'b0}}),
    .in5({5{1'b0}}), .in6({5{1'b0}}), .in7({5{1'b0}}), .out(raddr1), .sel(select_signal));
  Multiplexer #(.select(3), .width(5)) multiplexer_2 (
    .in0(addi_raddr2), .in1(jalr_raddr2), .in2(add_raddr2), .in3({5{1'b0}}), .in4({5{1'b0}}),
    .in5({5{1'b0}}), .in6({5{1'b0}}), .in7({5{1'b0}}), .out(raddr2), .sel(select_signal));
  Multiplexer #(.select(3), .width(5)) multiplexer_3 (
    .in0(addi_waddr), .in1(jalr_waddr), .in2(add_waddr), .in3({5{1'b0}}), .in4({5{1'b0}}), .in5({5{1'b0}}),
    .in6({5{1'b0}}), .in7({5{1'b0}}), .out(waddr), .sel(select_signal));
  Multiplexer #(.select(3)) multiplexer_4 (
    .in0(addi_wenable), .in1(jalr_wenable), .in2(add_wenable), .in3(1'b0), .in4(1'b0), .in5(1'b0),
    .in6(1'b0), .in7(1'b0), .out(wenable), .sel(select_signal));
  Multiplexer #(.select(3), .width(32)) multiplexer_5 (
    .in0(addi_wdata), .in1(jalr_wdata), .in2(add_wdata), .in3({32{1'b0}}), .in4({32{1'b0}}),
    .in5({32{1'b0}}), .in6({32{1'b0}}), .in7({32{1'b0}}), .out(wdata), .sel(select_signal));
  Multiplexer #(.select(3), .width(32)) multiplexer_6 (
    .in0(addi_jump_addr), .in1(jalr_jump_addr), .in2(add_jump_addr), .in3({32{1'b0}}), .in4({32{1'b0}}),
    .in5({32{1'b0}}), .in6({32{1'b0}}), .in7({32{1'b0}}), .out(jump_addr), .sel(select_signal));
  Multiplexer #(.select(3)) multiplexer_7 (
    .in0(addi_jump_enable), .in1(jalr_jump_enable), .in2(add_jump_enable), .in3(1'b0), .in4(1'b0),
    .in5(1'b0), .in6(1'b0), .in7(1'b0), .out(jump_enable), .sel(select_signal));
  Multiplexer #(.width(3)) multiplexer_8 (
    .in0(3'b000), .in1(priority_encoder_1_out), .out(select_signal), .sel(or_1_out));
endmodule

module addi_executor (
  input  [31:0] instruction,
  input  [31:0] rdata1,
  output [4:0] raddr1,
  output [4:0] raddr2,
  output [4:0] waddr,
  output wenable,
  output [31:0] wdata,
  output [31:0] jump_addr,
  output jump_enable
);

  wire [11:0] instruction_decoder_1_imm;
  wire [31:0] bit_extender_1_out;

  instruction_decoder instruction_decoder_1 (
    .instrction(instruction), .rd(waddr), .rs1(raddr1), .imm(instruction_decoder_1_imm));  // open: opcode, funct3, funct7, rs2
  assign bit_extender_1_out = {{20{instruction_decoder_1_imm[11]}}, instruction_decoder_1_imm};  // Bit_Extender bit_extender_1
  Adder #(.width(32)) adder_1 (.a(bit_extender_1_out), .b(rdata1), .out(wdata));  // open: cin, cout

  assign jump_addr = {32{1'b0}};
  assign jump_enable = 1'b0;
  assign raddr2 = {5{1'b0}};
  assign wenable = 1'b1;
endmodule

module jalr_excutor (
  input  [31:0] instruction,
  input  [31:0] rdata1,
  input  [31:0] next_addr,
  output [4:0] raddr1,
  output [4:0] raddr2,
  output [4:0] waddr,
  output wenable,
  output [31:0] wdata,
  output [31:0] jump_addr,
  output jump_enable
);

  wire [11:0] instruction_decoder_1_imm;
  wire [31:0] bit_extender_1_out;

  instruction_decoder instruction_decoder_1 (
    .instrction(instruction), .rd(waddr), .rs1(raddr1), .imm(instruction_decoder_1_imm));  // open: opcode, funct3, funct7, rs2
  assign bit_extender_1_out = {{20{instruction_decoder_1_imm[11]}}, instruction_decoder_1_imm};  // Bit_Extender bit_extender_1
  Adder #(.width(32)) adder_1 (.a(bit_extender_1_out), .b(rdata1), .out(jump_addr));  // open: cin, cout

  assign jump_enable = 1'b1;
  assign raddr2 = {5{1'b0}};
  assign wdata = next_addr;
  assign wenable = 1'b1;
endmodule

module r_decoder (
  input  [31:0] instruction,
  output [6:0] opcode,
  output [4:0] rd,
  output [2:0] funct3,
  output [4:0] rs1,
  output [4:0] rs2,
  output [6:0] funct7,
  output [11:0] imm
);


  assign funct3 = instruction[14:12];
  assign funct7 = instruction[31:25];
  assign imm = {12{1'b0}};
  assign opcode = instruction[6:0];
  assign rd = instruction[11:7];
  assign rs1 = instruction[19:15];
  assign rs2 = instruction[24:20];
endmodule

module add_executor (
  input  [31:0] instruction,
  input  [31:0] rdata1,
  input  [31:0] rdata2,
  output [4:0] raddr1,
  output [4:0] raddr2,
  output [4:0] waddr,
  output wenable,
  output [31:0] wdata,
  output [31:0] jump_addr,
  output jump_enable
);

  Adder #(.width(32)) adder_1 (.a(rdata1), .b(rdata2), .out(wdata));  // open: cin, cout
  instruction_decoder instruction_decoder_1 (
    .instrction(instruction), .rd(waddr), .rs1(raddr1), .rs2(raddr2));  // open: opcode, funct3, imm, funct7

  assign jump_addr = {32{1'b0}};
  assign jump_enable = 1'b0;
  assign wenable = 1'b1;
endmodule
